// Logisim project sqrt2.circ as structural Verilog: 8 circuits, main circuit main
module main (
  input  ENABLE,
  input  [15:0] IO_DATA_IN,
  output NAN,
  output PINF,
  output NINF,
  output RESULT,
  output [15:0] IO_DATA_OUT
);

  wire CLK_out;

  Clock CLK (.out(CLK_out));
  sqrt sqrt_1 (
    .CLK(CLK_out), .ENABLE(ENABLE), .IO_DATA_IN(IO_DATA_IN), .IS_NAN(NAN), .IS_PINF(PINF), .IS_NINF(NINF),
    .RESULT(RESULT), .IO_DATA_OUT(IO_DATA_OUT));
endmodule

module sqrt (
  input  CLK,
  input  ENABLE,
  input  [15:0] IO_DATA_IN,
  output IS_NAN,
  output IS_PINF,
  output IS_NINF,
  output RESULT,
  output [15:0] IO_DATA_OUT
);


  assign IO_DATA_OUT = IO_DATA_IN;
endmodule

module sum1 (
  input  A,
  input  B,
  input  Cin,
  output S,
  output Cout
);

  wire and_1_out, and_2_out, xor_1_out;

  xor xor_1 (xor_1_out, A, B);
  xor xor_2 (S, xor_1_out, Cin);
  and and_1 (and_1_out, xor_1_out, Cin);
  and and_2 (and_2_out, A, B);
  or or_1 (Cout, and_1_out, and_2_out);
endmodule

module sum2 (
  input  [1:0] A,
  input  [1:0] B,
  input  Cin,
  output [1:0] S,
  output Cout
);

  wire sum1_1_cout;

  sum1 sum1_1 (.A(A[0]), .B(B[0]), .Cin(Cin), .S(S[0]), .Cout(sum1_1_cout));
  sum1 sum1_2 (.A(A[1]), .B(B[1]), .Cin(sum1_1_cout), .S(S[1]), .Cout(Cout));
endmodule

module sum4 (
  input  [3:0] A,
  input  [3:0] B,
  input  Cin,
  output [3:0] S,
  output Cout
);

  wire sum2_1_cout;

  sum2 sum2_1 (.A(A[1:0]), .B(B[1:0]), .Cin(Cin), .S(S[1:0]), .Cout(sum2_1_cout));
  sum2 sum2_2 (.A(A[3:2]), .B(B[3:2]), .Cin(sum2_1_cout), .S(S[3:2]), .Cout(Cout));

  // Other names for the same wires on the sheet: A1[1:0] = A[3:2]; B1[1:0] = B[3:2]
endmodule

module sum8 (
  input  [7:0] A,
  input  [7:0] B,
  input  Cin,
  output [7:0] S,
  output Cout
);

  wire sum4_1_cout;

  sum4 sum4_1 (.A(A[3:0]), .B(B[3:0]), .Cin(Cin), .S(S[3:0]), .Cout(sum4_1_cout));
  sum4 sum4_2 (.A(A[7:4]), .B(B[7:4]), .Cin(sum4_1_cout), .S(S[7:4]), .Cout(Cout));

  // Other names for the same wires on the sheet: A1[3:0] = A[7:4]; B1[3:0] = B[7:4]
endmodule

module sum16 (
  input  [15:0] A,
  input  [15:0] B,
  input  Cin,
  output [15:0] S,
  output Cout
);

  wire sum8_1_cout;

  sum8 sum8_1 (.A(A[7:0]), .B(B[7:0]), .Cin(Cin), .S(S[7:0]), .Cout(sum8_1_cout));
  sum8 sum8_2 (.A(A[15:8]), .B(B[15:8]), .Cin(sum8_1_cout), .S(S[15:8]), .Cout(Cout));

  // Other names for the same wires on the sheet: A1[7:0] = A[15:8]; B1[7:0] = B[15:8]
endmodule

module sum32 (
  input  [31:0] A,
  input  [31:0] B,
  input  Cin,
  output [31:0] S,
  output Cout
);

  wire sum16_1_cout;

  sum16 sum16_1 (.A(A[15:0]), .B(B[15:0]), .Cin(Cin), .S(S[15:0]), .Cout(sum16_1_cout));
  sum16 sum16_2 (.A(A[31:16]), .B(B[31:16]), .Cin(sum16_1_cout), .S(S[31:16]), .Cout(Cout));

  // Other names for the same wires on the sheet: A1[15:0] = A[31:16]; B1[15:0] = B[31:16]
endmodule
